# Fritzing sketch ASimpleIoTCircuitDiagram (saved by Fritzing 0.9.2b)
breadboards: 1

parts:
  LED1 = RGB LED (com. cathode, rbg) [package="5 mm [THT]"]
  IC1 = Single-Chip USB to UART Bridge [package=mlp28]
  R1 = Resistor [tolerance=±5% resistance=220 package=THT]
  R2 = Resistor [tolerance=±5% resistance=220 package=THT]
  R3 = Resistor [tolerance=±5% resistance=220 package=THT]
  S1 = Pushbutton [package="[THT]"]
  R4 = Resistor [tolerance=±5% resistance=10k package=THT]
  T1 = TMP36 Temperature Sensor [package="TO92 [THT]"]

nets:
  N1: LED1.red_anode, R1.Pin_0
  GND: LED1.common_cathode, IC1.GND, R4.Pin_0, T1.GND
  N2: LED1.blue_anode, R2.Pin_0
  N3: LED1.green_anode, R3.Pin_0
  N4: IC1.RI, S1.Pin_1, S1.Pin_2, T1.+Vs
  N5: IC1.!SUSPEND, R3.Pin_1, S1.Pin_3, S1.Pin_4, R4.Pin_1
  N6: IC1.GPIO_3, T1.Vout

notes:
  ESP8266-12E
  D1 - Blue (On/Off Switch, subscriber)
  D2 - Red (Slider, subscriber)
  D4 - Green (Physical button, publisher)
  GND
  3V3
  220 Ω
  10k Ω
  TMP36,
  Temperature sensor
